// Logisim project FULL_ADDER.circ as structural Verilog: 13 circuits, main circuit FULL_ADDER
module FULL_ADDER (
  input  A,
  input  B,
  input  Cin,
  output SUM,
  output Cout
);

  wire and_1_out, and_2_out, xor_1_out;

  xor xor_1 (xor_1_out, A, B);
  and and_1 (and_1_out, A, B);
  xor xor_2 (SUM, xor_1_out, Cin);
  and and_2 (and_2_out, xor_1_out, Cin);
  or or_1 (Cout, and_2_out, and_1_out);
endmodule

module ADD_3BIT (
  input  B2,
  input  B1,
  input  B0,
  input  A2,
  input  A1,
  input  A0,
  output S1,
  output S0,
  output S3,
  output S2
);

  wire full_adder_1_cout, full_adder_2_cout;

  FULL_ADDER full_adder_1 (.A(A0), .B(B0), .Cin(1'b0), .SUM(S0), .Cout(full_adder_1_cout));
  FULL_ADDER full_adder_2 (.A(A1), .B(B1), .Cin(full_adder_1_cout), .SUM(S1), .Cout(full_adder_2_cout));
  FULL_ADDER full_adder_3 (.A(A2), .B(B2), .Cin(full_adder_2_cout), .SUM(S2), .Cout(S3));

  // Notes on the sheet:
  //   FA0
  //   FA1
  //   FA2
endmodule

module NOT_3BIT (
  input  A2,
  input  A1,
  input  A0,
  output nA2,
  output nA1,
  output nA0
);

  not not_1 (nA0, A0);
  not not_2 (nA1, A1);
  not not_3 (nA2, A2);
endmodule

module TWOS_COMPLEMENT (
  input  A2,
  input  A1,
  input  A0,
  output B3,
  output B2,
  output B1,
  output B0
);

  wire not_3bit_1_na0, not_3bit_1_na1, not_3bit_1_na2;

  NOT_3BIT not_3bit_1 (.A2(A2), .A1(A1), .A0(A0), .nA2(not_3bit_1_na2), .nA1(not_3bit_1_na1), .nA0(not_3bit_1_na0));
  ADD_3BIT add_3bit_1 (
    .B2(1'b0), .B1(1'b0), .B0(1'b1), .A2(not_3bit_1_na2), .A1(not_3bit_1_na1), .A0(not_3bit_1_na0), .S3(B3),
    .S2(B2), .S1(B1), .S0(B0));
endmodule

module SUB_3BIT (
  input  B2,
  input  B1,
  input  B0,
  input  A2,
  input  A1,
  input  A0,
  output Y3,
  output Y2,
  output Y1,
  output Y0
);

  wire twos_complement_1_b0, twos_complement_1_b1, twos_complement_1_b2;

  TWOS_COMPLEMENT twos_complement_1 (
    .A2(B2), .A1(B1), .A0(B0), .B2(twos_complement_1_b2), .B1(twos_complement_1_b1), .B0(twos_complement_1_b0));  // open: B3
  ADD_3BIT add_3bit_1 (
    .B2(A2), .B1(A1), .B0(A0), .A2(twos_complement_1_b2), .A1(twos_complement_1_b1),
    .A0(twos_complement_1_b0), .S3(Y3), .S2(Y2), .S1(Y1), .S0(Y0));
endmodule

module AND_3BIT (
  input  B2,
  input  B1,
  input  B0,
  input  A2,
  input  A1,
  input  A0,
  output Y2,
  output Y1,
  output Y0
);

  and and_1 (Y0, A0, B0);
  and and_2 (Y1, A1, B1);
  and and_3 (Y2, A2, B2);
endmodule

module OR_3BIT (
  input  B2,
  input  B1,
  input  B0,
  input  A2,
  input  A1,
  input  A0,
  output Y2,
  output Y1,
  output Y0
);

  or or_1 (Y0, A0, B0);
  or or_2 (Y1, A1, B1);
  or or_3 (Y2, A2, B2);
endmodule

module XOR_3BIT (
  input  B2,
  input  B1,
  input  B0,
  input  A2,
  input  A1,
  input  A0,
  output Y2,
  output Y1,
  output Y0
);

  xor xor_1 (Y0, A0, B0);
  xor xor_2 (Y1, A1, B1);
  xor xor_3 (Y2, A2, B2);
endmodule

module SHIFT_LEFT_2 (
  input  A2,
  input  A1,
  input  A0,
  output Y4,
  output Y3,
  output Y2,
  output Y1,
  output Y0
);


  assign Y0 = 1'b0;
  assign Y1 = 1'b0;
  assign Y2 = A0;
  assign Y3 = A1;
  assign Y4 = A2;
endmodule

module SHIFT_RIGHT_3 (
  input  A2,
  input  A1,
  input  A0,
  output Y4,
  output Y3,
  output Y2,
  output Y1,
  output Y0
);


  assign Y0 = A2;
  assign Y1 = 1'b0;
  assign Y2 = 1'b0;
  assign Y3 = 1'b0;
  assign Y4 = 1'b0;
endmodule

module SHIFT_RIGHT_ARITH_1 (
  input  A2,
  input  A1,
  input  A0,
  output Y2,
  output Y1,
  output Y0
);


  assign Y0 = A1;
  assign Y1 = A2;
  assign Y2 = A2;
endmodule

module SHIFT_LEFT_ARITH_1 (
  input  A2,
  input  A1,
  input  A0,
  output Y2,
  output Y1,
  output Y0
);


  assign Y0 = 1'b0;
  assign Y1 = A0;
  assign Y2 = A1;
endmodule

module ALU_TOP (
  input  B2,
  input  B1,
  input  B0,
  input  A2,
  input  A1,
  input  A0,
  input  [3:0] Sel,
  output [4:0] out_8,
  output out_9,
  output [2:0] out_10
);

  wire [1:0] not_1_out, undriven;
  wire [4:0] shift_left_2_1_y0, shift_right_3_1_y0, undriven_2, undriven_3, undriven_4, undriven_5,
       undriven_6, undriven_7, undriven_8, undriven_9;
  wire [4:3] add_3bit_1_s1;

  ADD_3BIT add_3bit_1 (
    .B2(B2), .B1(B1), .B0(B0), .A2(A2), .A1(A1), .A0(A0), .S3(out_9), .S2(add_3bit_1_s1[4]),
    .S1(add_3bit_1_s1[3]), .S0(add_3bit_1_s1[3]));
  SUB_3BIT sub_3bit_1 (
    .B2(B2), .B1(B1), .B0(B0), .A2(A2), .A1(A1), .A0(A0), .Y3(undriven_2[4]), .Y2(undriven_2[3]),
    .Y1(undriven_2[2]), .Y0(undriven_2[1]));
  TWOS_COMPLEMENT twos_complement_1 (
    .A2(B2), .A1(B1), .A0(B0), .B2(undriven_3[4]), .B1(undriven_3[3]), .B0(undriven_3[2]));  // open: B3
  OR_3BIT or_3bit_1 (
    .B2(B2), .B1(B1), .B0(B0), .A2(A2), .A1(A1), .A0(A0), .Y2(undriven_4[4]), .Y1(undriven_4[3]),
    .Y0(undriven_4[2]));
  AND_3BIT and_3bit_1 (
    .B2(B2), .B1(B1), .B0(B0), .A2(A2), .A1(A1), .A0(A0), .Y2(undriven_5[4]), .Y1(undriven_5[3]),
    .Y0(undriven_5[2]));
  XOR_3BIT xor_3bit_1 (
    .B2(B2), .B1(B1), .B0(B0), .A2(A2), .A1(A1), .A0(A0), .Y2(undriven_6[4]), .Y1(undriven_6[3]),
    .Y0(undriven_6[2]));
  NOT_3BIT not_3bit_1 (.A2(A2), .A1(A1), .A0(A0), .nA2(undriven_7[4]), .nA1(undriven_7[3]), .nA0(undriven_7[2]));
  SHIFT_LEFT_2 shift_left_2_1 (
    .A2(A2), .A1(A1), .A0(A0), .Y4(shift_left_2_1_y0[4]), .Y3(shift_left_2_1_y0[3]),
    .Y2(shift_left_2_1_y0[2]), .Y1(shift_left_2_1_y0[1]), .Y0(shift_left_2_1_y0[0]));
  SHIFT_RIGHT_3 shift_right_3_1 (
    .A2(A2), .A1(A1), .A0(A0), .Y4(shift_right_3_1_y0[4]), .Y3(shift_right_3_1_y0[3]),
    .Y2(shift_right_3_1_y0[2]), .Y1(shift_right_3_1_y0[1]), .Y0(shift_right_3_1_y0[0]));
  SHIFT_RIGHT_ARITH_1 shift_right_arith_1_1 (
    .A2(A2), .A1(A1), .A0(A0), .Y2(undriven_8[4]), .Y1(undriven_8[3]), .Y0(undriven_8[2]));
  SHIFT_LEFT_ARITH_1 shift_left_arith_1_1 (
    .A2(A2), .A1(A1), .A0(A0), .Y2(undriven_9[4]), .Y1(undriven_9[3]), .Y0(undriven_9[2]));
  Multiplexer #(.select(4), .width(5), .enable("false")) multiplexer_1 (
    .in0({add_3bit_1_s1, add_3bit_1_s1[3], undriven}), .in1(undriven_2), .in2(undriven_3), .in3(undriven_4),
    .in4(undriven_5), .in5(undriven_6), .in6(undriven_7), .in7(shift_left_2_1_y0), .in8(shift_right_3_1_y0),
    .in9(undriven_8), .in10(undriven_9), .out(out_8), .sel(Sel));  // open: in11, in12, in13, in14, in15
  assign {out_10, not_1_out} = ~out_8;  // NOT_Gate not_1, 5 bits wide
endmodule
